# Fritzing sketch semaforo_v1 (saved by Fritzing 0.9.4)
breadboards: 1

parts:
  Componente1 = RFID-RC522 [part_number=101218]
  Componente2 = Arduino Mega 2560 (Rev3)
  S1 = Tactile Switch Buttons - 12mm Square [package=tactile-pth-12mm]
  LED1 = LED - 5mm [color="Red (633nm)" package="5 mm [THT]"]
  LED2 = LED - 5mm [color="Yellow (592nm)" package="5 mm [THT]"]
  LED3 = LED - 5mm [color="Green (565nm)" package="5 mm [THT]"]
  LED4 = LED - 5mm [color="Green (565nm)" package="5 mm [THT]"]
  LED5 = LED - 5mm [color="Red (633nm)" package="5 mm [THT]"]
  R1 = Resistor [tolerance=±5% resistance=220 package=THT]
  R2 = Resistor [tolerance=±5% resistance=220 package=THT]
  R3 = Resistor [tolerance=±5% resistance=220 package=THT]
  R4 = Resistor [tolerance=±5% resistance=220 package=THT]
  R5 = Resistor [tolerance=±5% resistance=220 package=THT]
  YL-83_-_Detection_Board1 = YL-83 Rain Sensor - Detection Board
  YL-83_-_Control_Board1 = YL-83 Rain Sensor - Control Board

nets:
  N1: Componente1.SDA, Componente2.D53
  N2: Componente1.SCK, Componente2.D52
  N3: Componente1.MOSI, Componente2.D51
  N4: Componente1.MISO, Componente2.D50
  GND: Componente1.GND, Componente2.GND, S1.1, S1.3, R1.Pin_0, R2.Pin_0, R3.Pin_0, R4.Pin_0, R5.Pin_0, YL-83_-_Control_Board1.GND
  N5: Componente1.RST, Componente2.D9_PWM
  3.3V: Componente1.3.3V, Componente2.3V3
  N6: Componente2.D8_PWM, YL-83_-_Control_Board1.DO
  5V: Componente2.5V, YL-83_-_Control_Board1.VCC
  N7: Componente2.D2_PWM, S1.2, S1.4
  N8: Componente2.D3_PWM, LED3.anode
  N9: Componente2.D4_PWM, LED5.anode
  N10: Componente2.D5_PWM, LED4.anode
  N11: Componente2.D6_PWM, LED2.anode
  N12: Componente2.D7_PWM, LED1.anode
  N13: LED1.cathode, R1.Pin_1
  N14: LED2.cathode, R2.Pin_1
  N15: LED3.cathode, R5.Pin_1
  N16: LED4.cathode, R3.Pin_1
  N17: LED5.cathode, R4.Pin_1
  N18: YL-83_-_Detection_Board1.POS, YL-83_-_Control_Board1.POS
  N19: YL-83_-_Detection_Board1.NEG, YL-83_-_Control_Board1.NEG

custom parts:
  Tactile Switch Buttons - 12mm Square: Medium-sized clicky momentary switches are standard input "buttons" on electronic projects. These work best in a PCB but can be used on a solderless breadboard as shown in this tutorial. The pins are normally open (disconnected) and when the button is pressed they are momentarily closed. They come in a pack of 10, they're pretty handy so you'll want to keep them around. You can find an EAGLE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
  YL-83 Rain Sensor - Detection Board: The YL-83 is a rain sensor that has more resistance when dry and less resistance when wet. The module runs at 5V.
  YL-83 Rain Sensor - Control Board: The YL-83 is a rain sensor that has more resistance when dry and less resistance when wet. The module runs at 5V.
